// Digital circuit ex_mem.dig as structural Verilog
module ex_mem (
  input  [1:0] WB,
  input  [2:0] M,
  input  [31:0] ba__in,
  input  [31:0] ar__in,
  input  z__in,
  input  [31:0] rd2__in,
  input  [4:0] dr__in,
  input  en,
  input  clk,
  output [1:0] WB__out,
  output [2:0] M__out,
  output [31:0] ba__out,
  output z__out,
  output [31:0] ar__out,
  output [31:0] rd2__out,
  output [4:0] dr__out
);

  Register #(.Bits(2)) register_1 (.D(WB), .C(clk), .en(en), .Q(WB__out));
  Register #(.Bits(3)) register_2 (.D(M), .C(clk), .en(en), .Q(M__out));
  Register #(.Bits(32)) register_3 (.D(ba__in), .C(clk), .en(en), .Q(ba__out));
  Register register_4 (.D(z__in), .C(clk), .en(en), .Q(z__out));
  Register #(.Bits(32)) register_5 (.D(ar__in), .C(clk), .en(en), .Q(ar__out));
  Register #(.Bits(32)) register_6 (.D(rd2__in), .C(clk), .en(en), .Q(rd2__out));
  Register #(.Bits(5)) register_7 (.D(dr__in), .C(clk), .en(en), .Q(dr__out));
endmodule
