// Digital circuit id_ex.dig as structural Verilog
module id_ex (
  input  clk,
  input  en,
  input  [1:0] WB,
  input  [2:0] M,
  input  [3:0] EX,
  input  [31:0] ip__in,
  input  [31:0] rd1__in,
  input  [31:0] rd2__in,
  input  [31:0] iv__in,
  input  [4:0] dr1__in,
  input  [4:0] dr2__in,
  output [1:0] WB__out,
  output [2:0] M__out,
  output [3:0] EX__out,
  output [31:0] ip__out,
  output [31:0] rd1__out,
  output [31:0] rd2__out,
  output [31:0] iv__out,
  output [4:0] dr1__out,
  output [4:0] dr2__out
);

  Register #(.Bits(2)) register_1 (.D(WB), .C(clk), .en(en), .Q(WB__out));
  Register #(.Bits(3)) register_2 (.D(M), .C(clk), .en(en), .Q(M__out));
  Register #(.Bits(4)) register_3 (.D(EX), .C(clk), .en(en), .Q(EX__out));
  Register #(.Bits(32)) register_4 (.D(ip__in), .C(clk), .en(en), .Q(ip__out));
  Register #(.Bits(32)) register_5 (.D(rd1__in), .C(clk), .en(en), .Q(rd1__out));
  Register #(.Bits(32)) register_6 (.D(rd2__in), .C(clk), .en(en), .Q(rd2__out));
  Register #(.Bits(32)) register_7 (.D(iv__in), .C(clk), .en(en), .Q(iv__out));
  Register #(.Bits(5)) register_8 (.D(dr1__in), .C(clk), .en(en), .Q(dr1__out));
  Register #(.Bits(5)) register_9 (.D(dr2__in), .C(clk), .en(en), .Q(dr2__out));
endmodule
