// Digital circuit if_id.dig as structural Verilog
module if_id (
  input  clk,
  input  en,
  input  [31:0] ip__in,
  input  [31:0] in__in,
  output [31:0] ip__out,
  output [31:0] in__out
);

  Register #(.Bits(32)) incr_pc (.D(ip__in), .C(clk), .en(en), .Q(ip__out));
  Register #(.Bits(32)) instruction (.D(in__in), .C(clk), .en(en), .Q(in__out));
endmodule
