// Digital circuit lab05_pipelined.dig as structural Verilog
module lab05_pipelined (
  input  clk,
  input  rst,
  output [31:0] PC,
  output [5:0] opcode,
  output [4:0] src1__addr,
  output [31:0] src1__out,
  output [4:0] src2__addr,
  output [31:0] src2__out,
  output [4:0] dst__addr,
  output [31:0] dst__data
);

  wire alu__src, br, EX_MEM_z__out, mem__read, mem__write, PCSrc, reg__dst, reg__write, u_alu_3_zero;
  wire [1:0] alu__op, EX_MEM_wb__out, ID_EX_wb__out, u_control_unit_alu_op, u_control_unit_reg_write;
  wire [1:1] MEM_WB_wb__out;
  wire [2:0] ID_EX_m__out, u_control_unit_branch;
  wire [3:0] u_alu_control_alu_control, u_control_unit_reg_dst;
  wire [4:0] EX_MEM_dr__out, ID_EX_dr1__out, ID_EX_dr2__out, multiplexer_3_out;
  wire [15:0] instr;
  wire [31:0] bitextender_1_out, branchAddr, cpumemory_d2, data__val, ID_EX_ip__out, ID_EX_iv__out,
       ID_EX_rd1__out, ID_EX_rd2__out, IF_ID_ip__out, incrPC, mem__addr, mem__data, MEM_WB_ar__out,
       MEM_WB_rd__out, multiplexer_1_out, multiplexer_2_out, u_alu_2_result, u_alu_3_result;

  Multiplexer #(.Bits(32)) multiplexer_1 (.sel(PCSrc), .in_0(incrPC), .in_1(branchAddr), .out(multiplexer_1_out));
  gen_register #(.applicationType("IVERILOG"), .CodeFile("./gen_register.v")) u_gen_register (
    .clk(clk), .rst(rst), .write_en(clk), .data_in(multiplexer_1_out), .data_out(PC));
  alu #(.applicationType("IVERILOG"), .CodeFile("./alu.v")) u_alu (
    .alu_control(4'b0010), .A(PC), .B(32'h4), .result(incrPC));  // open: zero
  RAMDualAccess #(.AddrBits(8), .isProgramMemory("true"), .Bits(32)) cpumemory (
    .str(mem__write), .C(clk), .ld(mem__read), .A1(mem__addr[7:0]), .Din1(mem__data), .A2(PC[9:2]),
    .D1(data__val), .D2(cpumemory_d2));
  if_id IF_ID (
    .clk(clk), .en(clk), .ip__in(incrPC), .in__in(cpumemory_d2), .ip__out(IF_ID_ip__out),
    .in__out({opcode, src1__addr, src2__addr, instr}));
  control_unit #(.applicationType("IVERILOG"), .CodeFile("./control_unit.v")) u_control_unit (
    .instr_op(opcode), .reg_write(u_control_unit_reg_write[0]), .mem_to_reg(u_control_unit_reg_write[1]),
    .branch(u_control_unit_branch[0]), .mem_read(u_control_unit_branch[1]),
    .mem_write(u_control_unit_branch[2]), .reg_dst(u_control_unit_reg_dst[0]),
    .alu_op(u_control_unit_alu_op), .alu_src(u_control_unit_reg_dst[3]));
  BitExtender #(.inputBits(16), .outputBits(32)) bitextender_1 (.in(instr), .out(bitextender_1_out));
  cpu_registers #(.applicationType("IVERILOG"), .CodeFile("./cpu_registers.v")) u_cpu_registers (
    .clk(clk), .rst(rst), .write_en(reg__write), .src1_addr(src1__addr), .src2_addr(src2__addr),
    .dst_addr(dst__addr), .data_in(dst__data), .src1_out(src1__out), .src2_out(src2__out));
  id_ex ID_EX (
    .clk(clk), .en(clk), .WB(u_control_unit_reg_write), .M(u_control_unit_branch),
    .EX({u_control_unit_reg_dst[3], u_control_unit_alu_op, u_control_unit_reg_dst[0]}),
    .ip__in(IF_ID_ip__out), .rd1__in(src1__out), .rd2__in(src2__out), .iv__in(bitextender_1_out),
    .dr1__in(src2__addr), .dr2__in(instr[15:11]), .WB__out(ID_EX_wb__out), .M__out(ID_EX_m__out),
    .EX__out({alu__src, alu__op, reg__dst}), .ip__out(ID_EX_ip__out), .rd1__out(ID_EX_rd1__out),
    .rd2__out(ID_EX_rd2__out), .iv__out(ID_EX_iv__out), .dr1__out(ID_EX_dr1__out), .dr2__out(ID_EX_dr2__out));
  Multiplexer #(.Bits(32)) multiplexer_2 (
    .sel(alu__src), .in_0(ID_EX_rd2__out), .in_1(ID_EX_iv__out), .out(multiplexer_2_out));
  Multiplexer #(.Bits(5)) multiplexer_3 (
    .sel(reg__dst), .in_0(ID_EX_dr1__out), .in_1(ID_EX_dr2__out), .out(multiplexer_3_out));
  alu_control #(.applicationType("IVERILOG"), .CodeFile("./alu_control.v")) u_alu_control (
    .funct(ID_EX_iv__out[5:0]), .alu_op(alu__op), .alu_control(u_alu_control_alu_control));
  alu #(.applicationType("IVERILOG"), .CodeFile("./alu.v")) u_alu_2 (
    .alu_control(4'b0010), .A(ID_EX_ip__out), .B({ID_EX_iv__out[31:2], 2'b00}), .result(u_alu_2_result));  // open: zero
  alu #(.applicationType("IVERILOG"), .CodeFile("./alu.v")) u_alu_3 (
    .A(ID_EX_rd1__out), .B(multiplexer_2_out), .alu_control(u_alu_control_alu_control), .zero(u_alu_3_zero),
    .result(u_alu_3_result));
  ex_mem EX_MEM (
    .WB(ID_EX_wb__out), .M(ID_EX_m__out), .ba__in(u_alu_2_result), .z__in(u_alu_3_zero),
    .ar__in(u_alu_3_result), .rd2__in(ID_EX_rd2__out), .dr__in(multiplexer_3_out), .clk(clk), .en(clk),
    .WB__out(EX_MEM_wb__out), .M__out({mem__write, mem__read, br}), .ba__out(branchAddr),
    .z__out(EX_MEM_z__out), .ar__out(mem__addr), .rd2__out(mem__data), .dr__out(EX_MEM_dr__out));
  and and_1 (PCSrc, br, EX_MEM_z__out);
  mem_wb MEM_WB (
    .WB(EX_MEM_wb__out), .rd__in(data__val), .ar__in(mem__addr), .dr__in(EX_MEM_dr__out), .clk(clk),
    .en(clk), .WB__out({MEM_WB_wb__out[1], reg__write}), .rd__out(MEM_WB_rd__out), .ar__out(MEM_WB_ar__out),
    .dr__out(dst__addr));
  Multiplexer #(.Bits(32)) multiplexer_4 (
    .sel(MEM_WB_wb__out[1]), .in_0(MEM_WB_ar__out), .in_1(MEM_WB_rd__out), .out(dst__data));

  // Other names for the same wires on the sheet: instr[31:16] = {opcode, src1__addr, src2__addr};
  //   reg__data[31:0] = dst__data; src1[31:0] = src1__out; src2[31:0] = src2__out

  // Notes on the sheet:
  //   Inputs
  //   PC
  //   Outputs for testing
endmodule
