// Digital circuit mem_wb.dig as structural Verilog
module mem_wb (
  input  [1:0] WB,
  input  [31:0] rd__in,
  input  [31:0] ar__in,
  input  [4:0] dr__in,
  input  clk,
  input  en,
  output [1:0] WB__out,
  output [31:0] rd__out,
  output [31:0] ar__out,
  output [4:0] dr__out
);

  Register #(.Bits(2)) register_1 (.D(WB), .C(clk), .en(en), .Q(WB__out));
  Register #(.Bits(32)) register_2 (.D(rd__in), .C(clk), .en(en), .Q(rd__out));
  Register #(.Bits(32)) register_3 (.D(ar__in), .C(clk), .en(en), .Q(ar__out));
  Register #(.Bits(5)) register_4 (.D(dr__in), .C(clk), .en(en), .Q(dr__out));
endmodule
